// Logisim project ALU.circ as structural Verilog: 1 circuit, main circuit main
module main (
  input  [15:0] in_1,
  input  zx,
  input  nx,
  input  f,
  input  [15:0] in_5,
  input  no,
  input  in_7,
  input  ny,
  input  zy,
  input  [15:0] in_10,
  output zr,
  output ng,
  output [15:0] out_13
);

  wire OR8WAY_2_out, OR8WAY_out, OR_out;
  wire [15:0] adder_1_out, and_1_out, multiplexer_1_out, multiplexer_2_out, multiplexer_3_out,
       multiplexer_4_out, multiplexer_5_out, not_1_out, not_2_out, not_3_out;

  Multiplexer #(.width(16)) multiplexer_1 (.in0(in_1), .in1(in_5), .out(multiplexer_1_out), .sel(zx));  // open: en
  Multiplexer #(.width(16)) multiplexer_2 (.in0(in_10), .in1(in_5), .out(multiplexer_2_out), .sel(zy));  // open: en
  Multiplexer #(.width(16)) multiplexer_3 (
    .in0(multiplexer_1_out), .in1(not_1_out), .out(multiplexer_3_out), .sel(nx));  // open: en
  assign not_1_out = ~multiplexer_1_out;  // NOT_Gate not_1, 16 bits wide
  Multiplexer #(.width(16)) multiplexer_4 (
    .in0(multiplexer_2_out), .in1(not_2_out), .out(multiplexer_4_out), .sel(ny));  // open: en
  assign not_2_out = ~multiplexer_2_out;  // NOT_Gate not_2, 16 bits wide
  Adder #(.width(16)) adder_1 (.a(multiplexer_3_out), .b(multiplexer_4_out), .out(adder_1_out));  // open: cin, cout
  Multiplexer #(.width(16)) multiplexer_5 (
    .in0(and_1_out), .in1(adder_1_out), .out(multiplexer_5_out), .sel(f));  // open: en
  assign and_1_out = multiplexer_3_out & multiplexer_4_out;  // AND_Gate and_1, 16 bits wide
  Multiplexer #(.width(16)) multiplexer_6 (
    .in0(multiplexer_5_out), .in1(not_3_out), .out(out_13), .sel(no));  // open: en
  assign not_3_out = ~multiplexer_5_out;  // NOT_Gate not_3, 16 bits wide
  or OR8WAY (OR8WAY_out, out_13[0], out_13[1], out_13[2], out_13[3], out_13[4], out_13[5], out_13[6], out_13[7]);
  or OR8WAY_2 (OR8WAY_2_out, out_13[8], out_13[9], out_13[10], out_13[11], out_13[12], out_13[13], out_13[14], out_13[15]);
  or OR (OR_out, OR8WAY_out, OR8WAY_2_out);
  and AND_2 (ng, in_7, out_13[15]);
  not not_4 (zr, OR_out);

  // Notes on the sheet:
  //   X[16]
  //   Y[16]
  //   x1
  //   FALSE
  //   y1
  //   x2
  //   y2
  //   o2
  //   F
  //   o1
  //   NG
  //   out[16]
endmodule
