// Logisim project AND.circ as structural Verilog: 16 circuits, main circuit AND y XOR
module AND_y_XOR (
  input  a,
  input  b,
  input  in_3,
  input  in_4,
  output out,
  output out_6
);

  wire and_1_out, and_2_out, nand_1_out, not_1_out, not_2_out;

  nand nand_1 (nand_1_out, a, b);
  not not_1 (not_1_out, in_4);
  not not_2 (not_2_out, in_3);
  not not_3 (out, nand_1_out);
  and and_1 (and_1_out, not_1_out, in_3);
  and and_2 (and_2_out, not_2_out, in_4);
  or or_1 (out_6, and_1_out, and_2_out);

  // Notes on the sheet:
  //   AND
  //   XOr
  //   notAB
endmodule

module Nand (
  input  in_1,
  input  in_2,
  output out_3
);

  wire and_1_out;

  and and_1 (and_1_out, in_1, in_2);
  not not_1 (out_3, and_1_out);
endmodule

module Not (
  input  in_1,
  output out_2
);

  nand nand_1 (out_2, in_1, in_1);
endmodule

module Or (
  input  in_1,
  input  in_2,
  output out_3
);

  wire not_1_out, not_2_out;

  not not_1 (not_1_out, in_1);
  not not_2 (not_2_out, in_2);
  not nand_1 (out_3, not_1_out);  // NAND_Gate
endmodule

module Mux (
  input  a,
  input  b,
  input  sel,
  input  a_2,
  input  b_2,
  input  in_6,
  output out_7,
  output out_8
);

  wire and_1_out, and_2_out, and_3_out, and_4_out, and_5_out, and_6_out, and_7_out, and_8_out, and_9_out,
       not_1_out, not_2_out, not_3_out, not_4_out, or_2_out, or_4_out;

  not not_1 (not_1_out, in_6);
  and and_1 (and_1_out, not_1_out, a_2);
  and and_2 (and_2_out, b_2, in_6);
  or or_1 (out_7, and_1_out, and_2_out);
  not not_2 (not_2_out, a);
  not not_3 (not_3_out, b);
  not not_4 (not_4_out, sel);
  and and_3 (and_3_out, b, a);
  and and_4 (and_4_out, not_2_out, b);
  buf and_5 (and_5_out, not_4_out);  // AND_Gate
  and and_6 (and_6_out, and_4_out, sel);
  or or_2 (or_2_out, and_6_out, and_8_out);
  and and_7 (and_7_out, a, not_3_out);
  and and_8 (and_8_out, and_7_out, not_4_out);
  or or_3 (out_8, or_2_out, or_4_out);
  and and_9 (and_9_out, and_3_out, sel);
  or or_4 (or_4_out, and_5_out, and_9_out);

  // Notes on the sheet:
  //   sel
endmodule

module Demux (
  input  in_1,
  input  in_2,
  output out_3,
  output out_4
);

  wire not_1_out;

  not not_1 (not_1_out, in_2);
  and and_1 (out_4, in_1, in_2);
  and and_2 (out_3, in_1, not_1_out);
endmodule

module Not16 (
  input  [15:0] in_1,
  output [15:0] out_2
);

  assign out_2 = ~in_1;  // NOT_Gate not_1, 16 bits wide
endmodule

module AND16 (
  input  [15:0] in_1,
  input  [15:0] in_2,
  input  [15:0] in_3,
  input  [15:0] in_4,
  output [15:0] out_5,
  output [15:0] out_6
);

  wire [15:0] nand_1_out;

  assign out_6 = in_3 & in_4;  // AND_Gate and_1, 16 bits wide
  assign nand_1_out = ~(in_1 & in_2);  // NAND_Gate nand_1, 16 bits wide
  assign out_5 = ~nand_1_out;  // NOT_Gate not_1, 16 bits wide
endmodule

module or16 (
  input  [15:0] in_1,
  input  [15:0] in_2,
  output [15:0] out_3
);

  assign out_3 = in_1 | in_2;  // OR_Gate or_1, 16 bits wide
endmodule

module Mux16 (
  input  [15:0] a,
  input  [15:0] in_2,
  input  [15:0] in_3,
  output [15:0] out_4
);

  wire [15:0] and_1_out, and_2_out, not_1_out;

  assign not_1_out = ~in_3;  // NOT_Gate not_1, 16 bits wide
  assign and_1_out = not_1_out & a;  // AND_Gate and_1, 16 bits wide
  assign and_2_out = in_2 & in_3;  // AND_Gate and_2, 16 bits wide
  assign out_4 = and_1_out | and_2_out;  // OR_Gate or_1, 16 bits wide

  // Notes on the sheet:
  //   b
  //   sel
endmodule

module Dmux16 (
  input  [15:0] in_1,
  input  [15:0] in_2,
  output [15:0] out_3,
  output [15:0] out_4
);

  wire [15:0] not_1_out;

  assign not_1_out = ~in_2;  // NOT_Gate not_1, 16 bits wide
  assign out_4 = in_1 & in_2;  // AND_Gate and_1, 16 bits wide
  assign out_3 = in_1 & not_1_out;  // AND_Gate and_2, 16 bits wide
endmodule

module Or8way (
  input  [7:0] in_1,
  output out_2
);

  wire or_1_out, or_2_out, or_3_out, or_4_out, or_5_out, or_6_out;

  or or_1 (or_1_out, in_1[0], in_1[1]);
  or or_2 (or_2_out, in_1[2], in_1[3]);
  or or_3 (or_3_out, in_1[4], in_1[5]);
  or or_4 (or_4_out, in_1[6], in_1[7]);
  or or_5 (or_5_out, or_1_out, or_2_out);
  or or_6 (or_6_out, or_3_out, or_4_out);
  or or_7 (out_2, or_5_out, or_6_out);
endmodule

module Mux4way16 (
  input  [15:0] in_1,
  input  [15:0] in_2,
  input  [15:0] in_3,
  input  [15:0] in_4,
  input  [1:0] in_5,
  output [15:0] out_6
);

  Multiplexer #(.select(2), .width(16)) multiplexer_1 (
    .in0(in_1), .in1(in_2), .in2(in_3), .in3(in_4), .out(out_6), .sel(in_5));  // open: en
endmodule

module Mux8way16 (
  input  [15:0] in_1,
  input  [15:0] in_2,
  input  [15:0] in_3,
  input  [15:0] in_4,
  input  [1:0] in_5,
  input  [15:0] in_6,
  input  [15:0] in_7,
  input  [15:0] in_8,
  input  [15:0] in_9,
  input  in_10,
  input  [1:0] in_11,
  output [15:0] out_12
);

  wire [15:0] multiplexer_1_out, multiplexer_2_out;

  Multiplexer #(.select(2), .width(16)) multiplexer_1 (
    .in0(in_1), .in1(in_2), .in2(in_3), .in3(in_4), .out(multiplexer_1_out), .sel(in_5));  // open: en
  Multiplexer #(.select(2), .width(16)) multiplexer_2 (
    .in1(in_7), .in2(in_8), .in3(in_9), .out(multiplexer_2_out), .sel(in_11));  // open: in0, en
  Multiplexer #(.width(16)) multiplexer_3 (
    .in0(multiplexer_1_out), .in1(multiplexer_2_out), .out(out_12), .sel(in_10));  // open: en
endmodule

module Dmux4way (
  input  in_1,
  input  [1:0] in_2,
  output out_3,
  output out_4,
  output out_5,
  output out_6
);

  Demultiplexer #(.select(2)) demultiplexer_1 (
    .out0(out_3), .out1(out_4), .out2(out_5), .out3(out_6), .in(in_1), .sel(in_2));  // open: en
endmodule

module Dmux8way (
  input  in_1,
  input  [2:0] in_2,
  output out_3,
  output out_4,
  output out_5,
  output out_6,
  output out_7,
  output out_8,
  output out_9,
  output out_10
);

  Demultiplexer #(.select(3)) demultiplexer_1 (
    .out0(out_3), .out1(out_4), .out2(out_5), .out3(out_6), .out4(out_7), .out5(out_8), .out6(out_9),
    .out7(out_10), .in(in_1), .sel(in_2));  // open: en
endmodule
