// Logisim project Inc16.circ as structural Verilog: 1 circuit, main circuit main
module main (
  input  in_1,
  input  in_2,
  input  in_3,
  input  in_4,
  input  in_5,
  input  in_6,
  input  in_7,
  input  in_8,
  input  in_9,
  input  [15:0] in_10,
  input  in_11,
  input  in_12,
  input  in_13,
  input  in_14,
  input  in_15,
  input  in_16,
  input  in_17,
  input  in_18,
  output [15:0] out_19
);

  wire adder_1_cout, adder_2_cout, adder_3_cout, adder_4_cout, adder_5_cout, adder_6_cout, adder_7_cout,
       adder_8_cout, adder_9_cout, adder_10_cout, adder_11_cout, adder_12_cout, adder_13_cout, adder_14_cout,
       adder_15_cout;

  Adder #(.width(1)) adder_1 (.a(in_2), .b(in_10[0]), .out(out_19[0]), .cin(in_1), .cout(adder_1_cout));
  Adder #(.width(1)) adder_2 (.a(adder_1_cout), .b(in_10[1]), .out(out_19[1]), .cin(in_3), .cout(adder_2_cout));
  Adder #(.width(1)) adder_3 (.a(adder_2_cout), .b(in_10[2]), .out(out_19[2]), .cin(in_4), .cout(adder_3_cout));
  Adder #(.width(1)) adder_4 (.a(adder_3_cout), .b(in_10[3]), .out(out_19[3]), .cin(in_5), .cout(adder_4_cout));
  Adder #(.width(1)) adder_5 (.a(adder_4_cout), .b(in_10[4]), .out(out_19[4]), .cin(in_6), .cout(adder_5_cout));
  Adder #(.width(1)) adder_6 (.a(adder_5_cout), .b(in_10[5]), .out(out_19[5]), .cin(in_7), .cout(adder_6_cout));
  Adder #(.width(1)) adder_7 (.a(adder_6_cout), .b(in_10[6]), .out(out_19[6]), .cin(in_8), .cout(adder_7_cout));
  Adder #(.width(1)) adder_8 (.a(adder_7_cout), .b(in_10[7]), .out(out_19[7]), .cin(in_9), .cout(adder_8_cout));
  Adder #(.width(1)) adder_9 (.a(adder_8_cout), .b(in_10[8]), .out(out_19[8]), .cin(in_11), .cout(adder_9_cout));
  Adder #(.width(1)) adder_10 (.a(adder_9_cout), .b(in_10[9]), .out(out_19[9]), .cin(in_12), .cout(adder_10_cout));
  Adder #(.width(1)) adder_11 (.a(adder_10_cout), .b(in_10[10]), .out(out_19[10]), .cin(in_13), .cout(adder_11_cout));
  Adder #(.width(1)) adder_12 (.a(adder_11_cout), .b(in_10[11]), .out(out_19[11]), .cin(in_14), .cout(adder_12_cout));
  Adder #(.width(1)) adder_13 (.a(adder_12_cout), .b(in_10[12]), .out(out_19[12]), .cin(in_15), .cout(adder_13_cout));
  Adder #(.width(1)) adder_14 (.a(adder_13_cout), .b(in_10[13]), .out(out_19[13]), .cin(in_16), .cout(adder_14_cout));
  Adder #(.width(1)) adder_15 (.a(adder_14_cout), .b(in_10[14]), .out(out_19[14]), .cin(in_17), .cout(adder_15_cout));
  Adder #(.width(1)) adder_16 (.a(adder_15_cout), .b(in_10[15]), .out(out_19[15]), .cin(in_18));  // open: cout

  // Notes on the sheet:
  //   IN[16]
  //   OUTPUT[16]
endmodule
