// Logisim project Proyecto2Nnd2ttrs.circ as structural Verilog: 3 circuits, main circuit sumador binario 
module sumador_binario (
  input  in_1,
  input  in_2,
  input  in_3,
  input  in_4,
  input  in_5,
  input  in_6,
  input  in_7,
  input  in_8,
  output out_9,
  output out_10,
  output out_11,
  output out_12,
  output out_13,
  output out_14,
  output out_15,
  output out_16
);

  wire and_2_out, and_3_out, and_4_out, and_5_out, and_6_out, and_7_out, xor_2_out, xor_4_out, xor_6_out;

  xor xor_1 (out_9, in_1, in_2);
  and and_1 (out_10, in_1, in_2);
  xor xor_2 (xor_2_out, in_3, in_4);
  and and_2 (and_2_out, in_3, in_4);
  buf and_3 (and_3_out, xor_2_out);  // AND_Gate
  xor xor_3 (out_11, out_10, xor_2_out);
  or or_1 (out_12, and_3_out, and_2_out);
  xor xor_4 (xor_4_out, in_5, in_6);
  and and_4 (and_4_out, in_5, in_6);
  buf and_5 (and_5_out, xor_4_out);  // AND_Gate
  or or_2 (out_14, and_5_out, and_4_out);
  xor xor_5 (out_13, out_12, xor_4_out);
  xor xor_6 (xor_6_out, in_7, in_8);
  and and_6 (and_6_out, in_7, in_8);
  buf and_7 (and_7_out, xor_6_out);  // AND_Gate
  xor xor_7 (out_15, out_14, xor_6_out);
  or or_3 (out_16, and_7_out, and_6_out);
endmodule

module completo (
  input  in_1,
  input  in_2,
  input  in_3
);
endmodule

module add16 (
  input  [15:0] in_1,
  input  [15:0] in_2,
  output out_3,
  output out_4,
  output out_5,
  output out_6,
  output out_7,
  output out_8,
  output out_9,
  output out_10,
  output out_11,
  output out_12,
  output out_13,
  output out_14,
  output out_15,
  output out_16,
  output out_17,
  output out_18,
  output out_19
);

  wire adder_1_cout, adder_2_cout, adder_4_cout, adder_5_cout, adder_6_cout, adder_7_cout, adder_8_cout,
       adder_9_cout, adder_10_cout, adder_11_cout, adder_12_cout, adder_13_cout, adder_14_cout, adder_15_cout;

  and and_1 (out_4, in_1[0], in_2[0]);
  xor xor_1 (out_3, in_1[0], in_2[0]);
  Adder #(.width(1)) adder_1 (.a(in_1[1]), .b(in_2[1]), .out(out_5), .cin(out_4), .cout(adder_1_cout));
  Adder #(.width(1)) adder_2 (.a(in_1[8]), .b(in_2[8]), .out(out_12), .cin(adder_14_cout), .cout(adder_2_cout));
  Adder #(.width(1)) adder_3 (.a(in_1[15]), .b(in_2[15]), .out(out_19), .cin(adder_15_cout));  // open: cout
  Adder #(.width(1)) adder_4 (.a(in_1[2]), .b(in_2[2]), .out(out_6), .cin(adder_1_cout), .cout(adder_4_cout));
  Adder #(.width(1)) adder_5 (.a(in_1[9]), .b(in_2[9]), .out(out_13), .cin(adder_2_cout), .cout(adder_5_cout));
  Adder #(.width(1)) adder_6 (.a(in_1[3]), .b(in_2[3]), .out(out_7), .cin(adder_4_cout), .cout(adder_6_cout));
  Adder #(.width(1)) adder_7 (.a(in_1[10]), .b(in_2[10]), .out(out_14), .cin(adder_5_cout), .cout(adder_7_cout));
  Adder #(.width(1)) adder_8 (.a(in_1[4]), .b(in_2[4]), .out(out_8), .cin(adder_6_cout), .cout(adder_8_cout));
  Adder #(.width(1)) adder_9 (.a(in_1[11]), .b(in_2[11]), .out(out_15), .cin(adder_7_cout), .cout(adder_9_cout));
  Adder #(.width(1)) adder_10 (.a(in_1[5]), .b(in_2[5]), .out(out_9), .cin(adder_8_cout), .cout(adder_10_cout));
  Adder #(.width(1)) adder_11 (.a(in_1[12]), .b(in_2[12]), .out(out_16), .cin(adder_9_cout), .cout(adder_11_cout));
  Adder #(.width(1)) adder_12 (.a(in_1[6]), .b(in_2[6]), .out(out_10), .cin(adder_10_cout), .cout(adder_12_cout));
  Adder #(.width(1)) adder_13 (.a(in_1[13]), .b(in_2[13]), .out(out_17), .cin(adder_11_cout), .cout(adder_13_cout));
  Adder #(.width(1)) adder_14 (.a(in_1[7]), .b(in_2[7]), .out(out_11), .cin(adder_12_cout), .cout(adder_14_cout));
  Adder #(.width(1)) adder_15 (.a(in_1[14]), .b(in_2[14]), .out(out_18), .cin(adder_13_cout), .cout(adder_15_cout));
endmodule
