// Logisim project Proyecto3.circ as structural Verilog: 7 circuits, main circuit ram8
module registro (
  input  in_1,
  input  [15:0] in_2,
  output out_3,
  output out_4,
  output out_5,
  output out_6,
  output out_7,
  output out_8,
  output out_9,
  output out_10,
  output out_11,
  output out_12,
  output out_13,
  output out_14,
  output out_15,
  output out_16,
  output out_17,
  output out_18
);

  wire clock_1_out, multiplexer_1_out, multiplexer_2_out, multiplexer_3_out, multiplexer_4_out,
       multiplexer_5_out, multiplexer_6_out, multiplexer_7_out, multiplexer_8_out, multiplexer_9_out,
       multiplexer_10_out, multiplexer_11_out, multiplexer_12_out, multiplexer_13_out, multiplexer_14_out,
       multiplexer_15_out, multiplexer_16_out;

  Multiplexer multiplexer_1 (.in0(out_3), .in1(in_2[15]), .out(multiplexer_1_out), .sel(in_1));  // open: en
  Multiplexer multiplexer_2 (.in0(out_11), .in1(in_2[7]), .out(multiplexer_2_out), .sel(in_1));  // open: en
  D_Flip_Flop d_ff_1 (.D(multiplexer_1_out), .Q(out_3));  // open: clk, Qn, preset, en, reset
  D_Flip_Flop d_ff_2 (.clk(clock_1_out), .D(multiplexer_2_out), .Q(out_11));  // open: Qn, preset, en, reset
  Multiplexer multiplexer_3 (.in0(out_12), .in1(in_2[6]), .out(multiplexer_3_out), .sel(in_1));  // open: en
  D_Flip_Flop d_ff_3 (.clk(clock_1_out), .D(multiplexer_4_out), .Q(out_4));  // open: Qn, preset, en, reset
  Multiplexer multiplexer_4 (.in0(out_4), .in1(in_2[14]), .out(multiplexer_4_out), .sel(in_1));  // open: en
  D_Flip_Flop d_ff_4 (.clk(clock_1_out), .D(multiplexer_3_out), .Q(out_12));  // open: Qn, preset, en, reset
  D_Flip_Flop d_ff_5 (.clk(clock_1_out), .D(multiplexer_5_out), .Q(out_5));  // open: Qn, preset, en, reset
  Multiplexer multiplexer_5 (.in0(out_5), .in1(in_2[13]), .out(multiplexer_5_out), .sel(in_1));  // open: en
  D_Flip_Flop d_ff_6 (.clk(clock_1_out), .D(multiplexer_6_out), .Q(out_13));  // open: Qn, preset, en, reset
  Multiplexer multiplexer_6 (.in0(out_13), .in1(in_2[5]), .out(multiplexer_6_out), .sel(in_1));  // open: en
  Clock clock_1 (.out(clock_1_out));
  D_Flip_Flop d_ff_7 (.clk(clock_1_out), .D(multiplexer_7_out), .Q(out_6));  // open: Qn, preset, en, reset
  Multiplexer multiplexer_7 (.in0(out_6), .in1(in_2[12]), .out(multiplexer_7_out), .sel(in_1));  // open: en
  D_Flip_Flop d_ff_8 (.clk(clock_1_out), .D(multiplexer_8_out), .Q(out_14));  // open: Qn, preset, en, reset
  Multiplexer multiplexer_8 (.in0(out_14), .in1(in_2[4]), .out(multiplexer_8_out), .sel(in_1));  // open: en
  D_Flip_Flop d_ff_9 (.clk(clock_1_out), .D(multiplexer_9_out), .Q(out_7));  // open: Qn, preset, en, reset
  Multiplexer multiplexer_9 (.in0(out_7), .in1(in_2[11]), .out(multiplexer_9_out), .sel(in_1));  // open: en
  D_Flip_Flop d_ff_10 (.clk(clock_1_out), .D(multiplexer_10_out), .Q(out_15));  // open: Qn, preset, en, reset
  Multiplexer multiplexer_10 (.in0(out_15), .in1(in_2[3]), .out(multiplexer_10_out), .sel(in_1));  // open: en
  Multiplexer multiplexer_11 (.in0(out_16), .in1(in_2[2]), .out(multiplexer_11_out), .sel(in_1));  // open: en
  D_Flip_Flop d_ff_11 (.clk(clock_1_out), .D(multiplexer_12_out), .Q(out_8));  // open: Qn, preset, en, reset
  Multiplexer multiplexer_12 (.in0(out_8), .in1(in_2[10]), .out(multiplexer_12_out), .sel(in_1));  // open: en
  D_Flip_Flop d_ff_12 (.clk(clock_1_out), .D(multiplexer_11_out), .Q(out_16));  // open: Qn, preset, en, reset
  Multiplexer multiplexer_13 (.in0(out_9), .in1(in_2[9]), .out(multiplexer_13_out), .sel(in_1));  // open: en
  Multiplexer multiplexer_14 (.in0(out_17), .in1(in_2[1]), .out(multiplexer_14_out), .sel(in_1));  // open: en
  D_Flip_Flop d_ff_13 (.clk(clock_1_out), .D(multiplexer_13_out), .Q(out_9));  // open: Qn, preset, en, reset
  D_Flip_Flop d_ff_14 (.clk(clock_1_out), .D(multiplexer_14_out), .Q(out_17));  // open: Qn, preset, en, reset
  D_Flip_Flop d_ff_15 (.clk(clock_1_out), .D(multiplexer_15_out), .Q(out_10));  // open: Qn, preset, en, reset
  Multiplexer multiplexer_15 (.in0(out_10), .in1(in_2[8]), .out(multiplexer_15_out), .sel(in_1));  // open: en
  D_Flip_Flop d_ff_16 (.clk(clock_1_out), .D(multiplexer_16_out), .Q(out_18));  // open: Qn, preset, en, reset
  Multiplexer multiplexer_16 (.in0(out_18), .in1(in_2[0]), .out(multiplexer_16_out), .sel(in_1));  // open: en
endmodule

module Bit (
  input  in_1,
  input  LOAD,
  output out_3
);

  wire clock_1_out, multiplexer_1_out;

  Multiplexer multiplexer_1 (.in0(out_3), .in1(in_1), .out(multiplexer_1_out), .sel(LOAD));  // open: en
  Clock clock_1 (.out(clock_1_out));
  D_Flip_Flop d_ff_1 (.clk(clock_1_out), .D(multiplexer_1_out), .Q(out_3));  // open: Qn, preset, en, reset

  // Notes on the sheet:
  //   IN
  //   DFF
endmodule

module ram8 (
  input  [15:0] in_1,
  input  in_2,
  input  [2:0] in_3,
  output [15:0] out_4
);

  wire clock_1_out, demultiplexer_1_out0, demultiplexer_1_out1, demultiplexer_1_out2, demultiplexer_1_out3,
       demultiplexer_1_out4, demultiplexer_1_out5, demultiplexer_1_out6, demultiplexer_1_out7;
  wire [15:0] multiplexer_1_out, multiplexer_2_out, register_1_q, register_2_q, register_3_q, register_4_q,
       register_5_q, register_6_q, register_7_q, register_8_q;

  Demultiplexer #(.select(3)) demultiplexer_1 (
    .out0(demultiplexer_1_out0), .out1(demultiplexer_1_out1), .out2(demultiplexer_1_out2),
    .out3(demultiplexer_1_out3), .out4(demultiplexer_1_out4), .out5(demultiplexer_1_out5),
    .out6(demultiplexer_1_out6), .out7(demultiplexer_1_out7), .in(in_2), .sel(in_3));  // open: en
  Register #(.width(16)) register_1 (
    .D(in_1), .en(demultiplexer_1_out0), .Q(register_1_q), .clk(clock_1_out));  // open: clr
  Register #(.width(16)) register_2 (
    .D(in_1), .en(demultiplexer_1_out1), .Q(register_2_q), .clk(clock_1_out));  // open: clr
  Clock clock_1 (.out(clock_1_out));
  Register #(.width(16)) register_3 (
    .D(in_1), .en(demultiplexer_1_out2), .Q(register_3_q), .clk(clock_1_out));  // open: clr
  Register #(.width(16)) register_4 (
    .D(in_1), .en(demultiplexer_1_out3), .Q(register_4_q), .clk(clock_1_out));  // open: clr
  Register #(.width(16)) register_5 (
    .D(in_1), .en(demultiplexer_1_out4), .Q(register_5_q), .clk(clock_1_out));  // open: clr
  Register #(.width(16)) register_6 (
    .D(in_1), .en(demultiplexer_1_out5), .Q(register_6_q), .clk(clock_1_out));  // open: clr
  Register #(.width(16)) register_7 (
    .D(in_1), .en(demultiplexer_1_out6), .Q(register_7_q), .clk(clock_1_out));  // open: clr
  Register #(.width(16)) register_8 (
    .D(in_1), .en(demultiplexer_1_out7), .Q(register_8_q), .clk(clock_1_out));  // open: clr
  Multiplexer #(.select(2), .width(16)) multiplexer_1 (
    .in0(register_1_q), .in1(register_2_q), .in2(register_3_q), .in3(register_4_q), .out(multiplexer_1_out),
    .sel(in_3[1:0]));  // open: en
  Multiplexer #(.select(2), .width(16)) multiplexer_2 (
    .in0(register_5_q), .in1(register_6_q), .in2(register_7_q), .in3(register_8_q), .out(multiplexer_2_out),
    .sel(in_3[1:0]));  // open: en
  Multiplexer #(.width(16)) multiplexer_3 (
    .in0(multiplexer_1_out), .in1(multiplexer_2_out), .out(out_4), .sel(in_3[2]));  // open: en

  // Other names for the same wires on the sheet: sel_0_1[1:0] = in_3[1:0]; sel_2 = in_3[2]
endmodule

module Ram64 (
  input  [15:0] in_1,
  input  in_2,
  input  [5:0] in_3,
  output [15:0] out_4
);

  wire clock_1_out;
  wire [15:0] demultiplexer_1_out0, demultiplexer_1_out1, demultiplexer_1_out2, demultiplexer_1_out3,
       demultiplexer_1_out4, demultiplexer_1_out5, demultiplexer_1_out6, demultiplexer_1_out7, ram_1_data,
       ram_2_data, ram_3_data, ram_4_data, ram_5_data, ram_6_data, ram_7_data, ram_8_data;

  Demultiplexer #(.select(3), .width(16)) demultiplexer_1 (
    .out0(demultiplexer_1_out0), .out1(demultiplexer_1_out1), .out2(demultiplexer_1_out2),
    .out3(demultiplexer_1_out3), .out4(demultiplexer_1_out4), .out5(demultiplexer_1_out5),
    .out6(demultiplexer_1_out6), .out7(demultiplexer_1_out7), .in(in_1), .sel(in_3[5:3]), .en(in_2));
  RAM #(.addrWidth(3), .dataWidth(16), .bus("separate")) ram_1 (
    .addr(in_3[2:0]), .din(demultiplexer_1_out0), .data(ram_1_data), .sel(in_2), .clk(clock_1_out));  // open: str, ld, clr
  RAM #(.addrWidth(3), .dataWidth(16), .bus("separate")) ram_2 (
    .addr(in_3[2:0]), .din(demultiplexer_1_out1), .data(ram_2_data), .sel(in_2), .clk(clock_1_out));  // open: str, ld, clr
  RAM #(.addrWidth(3), .dataWidth(16), .bus("separate")) ram_3 (
    .addr(in_3[2:0]), .din(demultiplexer_1_out2), .data(ram_3_data), .sel(in_2), .clk(clock_1_out));  // open: str, ld, clr
  RAM #(.addrWidth(3), .dataWidth(16), .bus("separate")) ram_4 (
    .addr(in_3[2:0]), .din(demultiplexer_1_out3), .data(ram_4_data), .sel(in_2), .clk(clock_1_out));  // open: str, ld, clr
  Clock clock_1 (.out(clock_1_out));
  RAM #(.addrWidth(3), .dataWidth(16), .bus("separate")) ram_5 (
    .addr(in_3[2:0]), .din(demultiplexer_1_out4), .data(ram_5_data), .sel(in_2), .clk(clock_1_out));  // open: str, ld, clr
  RAM #(.addrWidth(3), .dataWidth(16), .bus("separate")) ram_6 (
    .addr(in_3[2:0]), .din(demultiplexer_1_out5), .data(ram_6_data), .sel(in_2), .clk(clock_1_out));  // open: str, ld, clr
  RAM #(.addrWidth(3), .dataWidth(16), .bus("separate")) ram_7 (
    .addr(in_3[2:0]), .din(demultiplexer_1_out6), .data(ram_7_data), .sel(in_2), .clk(clock_1_out));  // open: str, ld, clr
  RAM #(.addrWidth(3), .dataWidth(16), .bus("separate")) ram_8 (
    .addr(in_3[2:0]), .din(demultiplexer_1_out7), .data(ram_8_data), .sel(in_2), .clk(clock_1_out));  // open: str, ld, clr
  Multiplexer #(.select(3), .width(16)) multiplexer_1 (
    .in0(ram_1_data), .in1(ram_2_data), .in2(ram_3_data), .in3(ram_4_data), .in4(ram_5_data),
    .in5(ram_6_data), .in6(ram_7_data), .in7(ram_8_data), .out(out_4), .sel(in_3[5:3]), .en(in_2));
endmodule

module ram512 (
  input  [15:0] in_1,
  input  in_2,
  input  [8:0] in_3,
  output [15:0] out_4
);

  wire clock_1_out;
  wire [15:0] demultiplexer_1_out0, demultiplexer_1_out1, demultiplexer_1_out2, demultiplexer_1_out3,
       demultiplexer_1_out4, demultiplexer_1_out5, demultiplexer_1_out6, demultiplexer_1_out7, ram_1_data,
       ram_2_data, ram_3_data, ram_4_data, ram_5_data, ram_6_data, ram_7_data, ram_8_data;

  Demultiplexer #(.select(3), .width(16)) demultiplexer_1 (
    .out0(demultiplexer_1_out0), .out1(demultiplexer_1_out1), .out2(demultiplexer_1_out2),
    .out3(demultiplexer_1_out3), .out4(demultiplexer_1_out4), .out5(demultiplexer_1_out5),
    .out6(demultiplexer_1_out6), .out7(demultiplexer_1_out7), .in(in_1), .sel(in_3[8:6]), .en(in_2));
  RAM #(.addrWidth(6), .dataWidth(16), .bus("separate")) ram_1 (
    .addr(in_3[5:0]), .din(demultiplexer_1_out0), .data(ram_1_data), .sel(in_2), .clk(clock_1_out));  // open: str, ld, clr
  RAM #(.addrWidth(6), .dataWidth(16), .bus("separate")) ram_2 (
    .addr(in_3[5:0]), .din(demultiplexer_1_out1), .data(ram_2_data), .sel(in_2), .clk(clock_1_out));  // open: str, ld, clr
  RAM #(.addrWidth(6), .dataWidth(16), .bus("separate")) ram_3 (
    .addr(in_3[5:0]), .din(demultiplexer_1_out2), .data(ram_3_data), .sel(in_2), .clk(clock_1_out));  // open: str, ld, clr
  RAM #(.addrWidth(6), .dataWidth(16), .bus("separate")) ram_4 (
    .addr(in_3[5:0]), .din(demultiplexer_1_out3), .data(ram_4_data), .sel(in_2), .clk(clock_1_out));  // open: str, ld, clr
  Clock clock_1 (.out(clock_1_out));
  RAM #(.addrWidth(6), .dataWidth(16), .bus("separate")) ram_5 (
    .addr(in_3[5:0]), .din(demultiplexer_1_out4), .data(ram_5_data), .sel(in_2), .clk(clock_1_out));  // open: str, ld, clr
  RAM #(.addrWidth(6), .dataWidth(16), .bus("separate")) ram_6 (
    .addr(in_3[5:0]), .din(demultiplexer_1_out5), .data(ram_6_data), .sel(in_2), .clk(clock_1_out));  // open: str, ld, clr
  RAM #(.addrWidth(6), .dataWidth(16), .bus("separate")) ram_7 (
    .addr(in_3[5:0]), .din(demultiplexer_1_out6), .data(ram_7_data), .sel(in_2), .clk(clock_1_out));  // open: str, ld, clr
  RAM #(.addrWidth(6), .dataWidth(16), .bus("separate")) ram_8 (
    .addr(in_3[5:0]), .din(demultiplexer_1_out7), .data(ram_8_data), .sel(in_2), .clk(clock_1_out));  // open: str, ld, clr
  Multiplexer #(.select(3), .width(16)) multiplexer_1 (
    .in0(ram_1_data), .in1(ram_2_data), .in2(ram_3_data), .in3(ram_4_data), .in4(ram_5_data),
    .in5(ram_6_data), .in6(ram_7_data), .in7(ram_8_data), .out(out_4), .sel(in_3[8:6]), .en(in_2));
endmodule

module ram4k (
  input  [15:0] in_1,
  input  in_2,
  input  [11:0] in_3,
  output [15:0] out_4
);

  wire clock_1_out;
  wire [15:0] demultiplexer_1_out0, demultiplexer_1_out1, demultiplexer_1_out2, demultiplexer_1_out3,
       demultiplexer_1_out4, demultiplexer_1_out5, demultiplexer_1_out6, demultiplexer_1_out7, ram_1_data,
       ram_2_data, ram_3_data, ram_4_data, ram_5_data, ram_6_data, ram_7_data, ram_8_data;

  Demultiplexer #(.select(3), .width(16)) demultiplexer_1 (
    .out0(demultiplexer_1_out0), .out1(demultiplexer_1_out1), .out2(demultiplexer_1_out2),
    .out3(demultiplexer_1_out3), .out4(demultiplexer_1_out4), .out5(demultiplexer_1_out5),
    .out6(demultiplexer_1_out6), .out7(demultiplexer_1_out7), .in(in_1), .sel(in_3[11:9]), .en(in_2));
  RAM #(.addrWidth(9), .dataWidth(16), .bus("separate")) ram_1 (
    .addr(in_3[8:0]), .din(demultiplexer_1_out0), .data(ram_1_data), .sel(in_2), .clk(clock_1_out));  // open: str, ld, clr
  RAM #(.addrWidth(9), .dataWidth(16), .bus("separate")) ram_2 (
    .addr(in_3[8:0]), .din(demultiplexer_1_out1), .data(ram_2_data), .sel(in_2), .clk(clock_1_out));  // open: str, ld, clr
  RAM #(.addrWidth(9), .dataWidth(16), .bus("separate")) ram_3 (
    .addr(in_3[8:0]), .din(demultiplexer_1_out2), .data(ram_3_data), .sel(in_2), .clk(clock_1_out));  // open: str, ld, clr
  RAM #(.addrWidth(9), .dataWidth(16), .bus("separate")) ram_4 (
    .addr(in_3[8:0]), .din(demultiplexer_1_out3), .data(ram_4_data), .sel(in_2), .clk(clock_1_out));  // open: str, ld, clr
  Clock clock_1 (.out(clock_1_out));
  RAM #(.addrWidth(9), .dataWidth(16), .bus("separate")) ram_5 (
    .addr(in_3[8:0]), .din(demultiplexer_1_out4), .data(ram_5_data), .sel(in_2), .clk(clock_1_out));  // open: str, ld, clr
  RAM #(.addrWidth(9), .dataWidth(16), .bus("separate")) ram_6 (
    .addr(in_3[8:0]), .din(demultiplexer_1_out5), .data(ram_6_data), .sel(in_2), .clk(clock_1_out));  // open: str, ld, clr
  RAM #(.addrWidth(9), .dataWidth(16), .bus("separate")) ram_7 (
    .addr(in_3[8:0]), .din(demultiplexer_1_out6), .data(ram_7_data), .sel(in_2), .clk(clock_1_out));  // open: str, ld, clr
  RAM #(.addrWidth(9), .dataWidth(16), .bus("separate")) ram_8 (
    .addr(in_3[8:0]), .din(demultiplexer_1_out7), .data(ram_8_data), .sel(in_2), .clk(clock_1_out));  // open: str, ld, clr
  Multiplexer #(.select(3), .width(16)) multiplexer_1 (
    .in0(ram_1_data), .in1(ram_2_data), .in2(ram_3_data), .in3(ram_4_data), .in4(ram_5_data),
    .in5(ram_6_data), .in6(ram_7_data), .in7(ram_8_data), .out(out_4), .sel(in_3[11:9]), .en(in_2));
endmodule

module ram_16k (
  input  [15:0] in_1,
  input  in_2,
  input  [13:0] in_3,
  output [15:0] out_4
);

  wire clock_1_out;
  wire [15:0] demultiplexer_1_out0, demultiplexer_1_out1, demultiplexer_1_out2, demultiplexer_1_out3,
       ram_1_data, ram_2_data, ram_3_data, ram_4_data;

  Demultiplexer #(.select(2), .width(16)) demultiplexer_1 (
    .out0(demultiplexer_1_out0), .out1(demultiplexer_1_out1), .out2(demultiplexer_1_out2),
    .out3(demultiplexer_1_out3), .in(in_1), .sel(in_3[13:12]), .en(in_2));
  Clock clock_1 (.out(clock_1_out));
  RAM #(.addrWidth(12), .dataWidth(16), .bus("separate")) ram_1 (
    .addr(in_3[11:0]), .din(demultiplexer_1_out0), .data(ram_1_data), .sel(in_2), .clk(clock_1_out));  // open: str, ld, clr
  RAM #(.addrWidth(12), .dataWidth(16), .bus("separate")) ram_2 (
    .addr(in_3[11:0]), .din(demultiplexer_1_out1), .data(ram_2_data), .sel(in_2), .clk(clock_1_out));  // open: str, ld, clr
  RAM #(.addrWidth(12), .dataWidth(16), .bus("separate")) ram_3 (
    .addr(in_3[11:0]), .din(demultiplexer_1_out2), .data(ram_3_data), .sel(in_2), .clk(clock_1_out));  // open: str, ld, clr
  RAM #(.addrWidth(12), .dataWidth(16), .bus("separate")) ram_4 (
    .addr(in_3[11:0]), .din(demultiplexer_1_out3), .data(ram_4_data), .sel(in_2), .clk(clock_1_out));  // open: str, ld, clr
  Multiplexer #(.select(2), .width(16)) multiplexer_1 (
    .in0(ram_1_data), .in1(ram_2_data), .in2(ram_3_data), .in3(ram_4_data), .out(out_4), .sel(in_3[13:12]),
    .en(in_2));
endmodule
